# Fritzing sketch AnalogInputOutput (saved by Fritzing 1.0.8)
circuit board: 6.88566cm x 5.36311cm
breadboards: 2

parts:
  R4 = Resistor [resistance=220 tolerance=±5% power=0.25W package=THT]
  Arduino2 = Arduino Uno (Rev3)
  R5 = Rotary Potentiometer (Small) [maximum_resistance=10kΩ knob_status=50% power=0.5W package=THT]
  part = LED - 5mm [color="Red (633nm)" current=0.030A package="5 mm [THT]"]  # not connected

nets:
  N1: R4.Pin_1, Arduino2.D3_PWM
  N2: Arduino2.A3, R5.wiper
  N3: Arduino2.GND, R5.leg2
  N4: Arduino2.5V, R5.leg1

notes:
  In this example, potentiometer values are read in through an 'Analog In' pin. The values are then used to control the modulation of an LED on a PWM pin. Related examples: http://arduino.cc/en/Tutorial/AnalogInput http://arduino.cc/en/Tutorial/Fading
