# Fritzing sketch AnalogInputPot (saved by Fritzing 1.0.8)
circuit board: 6.88566cm x 5.36311cm
breadboards: 2

parts:
  Arduino2 = Arduino Uno (Rev3)
  R1 = Rotary Potentiometer (Small) [maximum_resistance=10kΩ knob_status=50% power=0.5W package=THT]
  part = LED - 5mm [color="Red (633nm)" current=0.030A package="5 mm [THT]"]  # not connected

nets:
  N1: Arduino2.A3, R1.wiper
  N2: Arduino2.GND, R1.leg1
  N3: Arduino2.5V, R1.leg2

notes:
  In this example, potentiometer values are read in through an 'Analog In' pin. The values are then used to control the blinking rate of an LED. Related example: http://arduino.cc/en/Tutorial/AnalogInput
