# Fritzing sketch AnalogInputThermistor (saved by Fritzing 1.0.8)
circuit board: 6.88566cm x 5.36311cm
breadboards: 2

parts:
  R3 = Resistor [resistance=1k tolerance=±5% power=0.25W package=THT]
  Arduino2 = Arduino Uno (Rev3)
  R4 = Temperature Sensor (Thermistor) [thermistor_type=NTC package=THT]
  part = LED - 5mm [color="Red (633nm)" current=0.030A package="5 mm [THT]"]  # not connected

nets:
  N1: R3.Pin_0, Arduino2.GND
  N2: R3.Pin_1, Arduino2.A2, R4.pin_1
  N3: Arduino2.5V, R4.pin_0

notes:
  In this example, thermistor values are read in through an 'Analog In' pin. The values are then used to control the blinking rate of an LED. Using a multimeter, check the min and max resistance of the thermistor in different light conditions. Then calculate the resistor's value with the Axel-Benz formula:
  Rref = sqrt(Rmin*Rmax)
  Related example: http://arduino.cc/en/Tutorial/AnalogInput
