# Fritzing sketch ArduinoISP (saved by Fritzing 1.0.8)
circuit board: 6.88566cm x 5.36311cm
breadboards: 2

parts:
  RESET1 = Pushbutton [package="[THT]"]
  R6 = Resistor [resistance=220 tolerance=±5% power=0.25W package=THT]
  R7 = Resistor [resistance=220 tolerance=±5% power=0.25W package=THT]
  R8 = Resistor [resistance=220 tolerance=±5% power=0.25W package=THT]
  R9 = Resistor [resistance=220 tolerance=±5% power=0.25W package=THT]
  ATMEGA1 = atmega168 [package=dip]
  R10 = Resistor [resistance=1k tolerance=±5% power=0.25W package=THT]
  Arduino1 = Arduino Uno (Rev3)
  Y1 = Resonator [frequency="16 Mhz" package=THT]
  part = LED - 5mm [color="Red (633nm)" current=0.030A package="5 mm [THT]"]  # not connected
  part_2 = LED - 5mm [color="Red (633nm)" current=0.030A package="5 mm [THT]"]  # not connected
  part_3 = LED - 5mm [color="Red (633nm)" current=0.030A package="5 mm [THT]"]  # not connected
  part_4 = LED - 5mm [color="Red (633nm)" current=0.030A package="5 mm [THT]"]  # not connected

nets:
  N1: RESET1.Pin_1, RESET1.Pin_2, ATMEGA1.RESET, R10.Pin_1, Arduino1.D10_PWM/SS
  GND: RESET1.Pin_3, RESET1.Pin_4, R6.Pin_0, R7.Pin_1, R8.Pin_1, R9.Pin_1, ATMEGA1.GND, Arduino1.GND, Y1.GND
  VCC: ATMEGA1.VCC, ATMEGA1.AVCC, R10.Pin_0, Arduino1.5V
  N2: ATMEGA1.XLAT1, Y1.0
  N3: ATMEGA1.XLAT2, Y1.pin_1
  N4: ATMEGA1.D11_(PWM), Arduino1.D11_PWM/MOSI
  N5: ATMEGA1.D12, Arduino1.D12/MISO
  N6: ATMEGA1.D13, Arduino1.D13/SCK

notes:
  Using an Arduino as ISP:
  http://arduino.cc/en/Tutorial/ArduinoISP
