# Fritzing sketch CosmicRayGun (saved by Fritzing 1.0.8)
circuit board: 6.88566cm x 5.36311cm
breadboards: 2

parts:
  R6 = Resistor [resistance=220 tolerance=±5% power=0.25W package=THT]
  R5 = Resistor [resistance=220 tolerance=±5% power=0.25W package=THT]
  R4 = Resistor [resistance=220 tolerance=±5% power=0.25W package=THT]
  R3 = Resistor [resistance=220 tolerance=±5% power=0.25W package=THT]
  R2 = Resistor [resistance=220 tolerance=±5% power=0.25W package=THT]
  R1 = Resistor [resistance=220 tolerance=±5% power=0.25W package=THT]
  S2 = Pushbutton [package=THT]
  R7 = Resistor [resistance=1k tolerance=±5% power=0.25W package=THT]
  R8 = Resistor [resistance=1k tolerance=±5% power=0.25W package=THT]
  S1 = Pushbutton [package=THT]
  Speaker = Piezo Speaker
  Arduino = Arduino Uno (Rev3)
  part = LED - 5mm [color="Red (633nm)" current=0.030A package="5 mm [THT]"]  # not connected
  part_2 = LED - 5mm [color="Red (633nm)" current=0.030A package="5 mm [THT]"]  # not connected
  part_3 = LED - 5mm [color="Red (633nm)" current=0.030A package="5 mm [THT]"]  # not connected
  part_4 = LED - 5mm [color="Red (633nm)" current=0.030A package="5 mm [THT]"]  # not connected
  part_5 = LED - 5mm [color="Red (633nm)" current=0.030A package="5 mm [THT]"]  # not connected
  part_6 = LED - 5mm [color="Red (633nm)" current=0.030A package="5 mm [THT]"]  # not connected

nets:
  N1: R6.Pin_0, Arduino.D7
  N2: R5.Pin_0, Arduino.D8
  N3: R4.Pin_0, Arduino.D9_PWM
  N4: R3.Pin_0, Arduino.D10_PWM/SS
  N5: R2.Pin_0, Arduino.D11_PWM/MOSI
  N6: R1.Pin_0, Arduino.D12/MISO
  N7: S2.leg0, S1.leg1, Arduino.5V
  N8: S2.leg1, R7.Pin_1, Arduino.D5_PWM
  N9: R7.Pin_0, R8.Pin_0, Arduino.GND
  N10: R8.Pin_1, S1.leg0, Arduino.D13/SCK
  N11: Speaker.pin1, Arduino.D2
  N12: Speaker.pin2, Arduino.D3_PWM

notes:
  Get the code from the Fritzing Project Page:
  Cosmic Raygun
