# Fritzing sketch FlipFlop (saved by Fritzing 1.0.8)
circuit board: 6.88566cm x 5.36311cm
breadboards: 2

parts:
  R3 = Resistor [tolerance=±5% resistance=100k power=0.25W package=THT]
  R1 = Resistor [tolerance=±5% resistance=220 power=0.25W package=THT]
  R2 = Resistor [tolerance=±5% resistance=220 power=0.25W package=THT]
  Button = Pushbutton [package=THT]
  Bauteil1 = Arduino Uno (Rev3)
  part = LED - 5mm [color="Red (633nm)" current=0.030A package="5 mm [THT]"]  # not connected
  part_2 = LED - 5mm [color="Red (633nm)" current=0.030A package="5 mm [THT]"]  # not connected

nets:
  N1: R3.Pin_0, Button.leg1, Bauteil1.D2
  N2: R3.Pin_1, Bauteil1.5V
  N3: R1.Pin_0, Bauteil1.D10_PWM/SS
  N4: R2.Pin_0, Bauteil1.D9_PWM
  N5: Button.leg0, Bauteil1.GND

notes:
  FLIP FLOP

// code stored in the sketch: FlipFlop.ino
/*
  Flip Flop
  schaltet mittels eines Tasters zwischen zwei LEDs hin und her
  
  Dieses Beispiel aus dem Fritzing Creator Kit: www.fritzing.org/creator-kit.
*/

int tasterPin=2;                       // Pin an dem der Taster angeschlossen ist
int grueneLED=9;                       // Pin an dem die grüne LED angeschlossen ist
int roteLED=10;                        // Pin an dem die rote LED angeschlossen ist 

void setup(){
  pinMode(tasterPin, INPUT);           // Taster Pin wird als INPUT initialisiert
  pinMode(grueneLED, OUTPUT);          // LED Pin wird als OUTPUT initialisiert
  pinMode(roteLED, OUTPUT);            // LED Pin wird als OUTPUT initialisiert 
}

void loop(){
  if (digitalRead(tasterPin)==LOW){    // wenn der Taster gedrückt ist (LOW) 
    digitalWrite(grueneLED, HIGH);     // grüne LED einschalten
    digitalWrite(roteLED, LOW);        // rote LED abschalten
  } else {                             // sonst
    digitalWrite(grueneLED, LOW);      // grüne LED abschalten
    digitalWrite(roteLED, HIGH);       // rote LED einschalten
  }
}
