# Fritzing sketch Lauflicht (saved by Fritzing 1.0.8)
circuit board: 6.88566cm x 5.36311cm
breadboards: 2

parts:
  R1 = Resistor [tolerance=±5% resistance=220 power=0.25W package=THT]
  R2 = Resistor [tolerance=±5% resistance=220 power=0.25W package=THT]
  R3 = Resistor [tolerance=±5% resistance=220 power=0.25W package=THT]
  R4 = Resistor [tolerance=±5% resistance=220 power=0.25W package=THT]
  R5 = Resistor [tolerance=±5% resistance=220 power=0.25W package=THT]
  R6 = Resistor [tolerance=±5% resistance=220 power=0.25W package=THT]
  R7 = Resistor [tolerance=±5% resistance=220 power=0.25W package=THT]
  R8 = Resistor [tolerance=±5% resistance=220 power=0.25W package=THT]
  Bauteil1 = Arduino Uno (Rev3)
  part = LED - 5mm [color="Red (633nm)" current=0.030A package="5 mm [THT]"]  # not connected
  part_2 = LED - 5mm [color="Red (633nm)" current=0.030A package="5 mm [THT]"]  # not connected
  part_3 = LED - 5mm [color="Red (633nm)" current=0.030A package="5 mm [THT]"]  # not connected
  part_4 = LED - 5mm [color="Red (633nm)" current=0.030A package="5 mm [THT]"]  # not connected
  part_5 = LED - 5mm [color="Red (633nm)" current=0.030A package="5 mm [THT]"]  # not connected
  part_6 = LED - 5mm [color="Red (633nm)" current=0.030A package="5 mm [THT]"]  # not connected
  part_7 = LED - 5mm [color="Red (633nm)" current=0.030A package="5 mm [THT]"]  # not connected
  part_8 = LED - 5mm [color="Red (633nm)" current=0.030A package="5 mm [THT]"]  # not connected

nets:
  N1: R1.Pin_0, Bauteil1.D9_PWM
  N2: R2.Pin_0, Bauteil1.D8
  N3: R3.Pin_0, Bauteil1.D7
  N4: R4.Pin_0, Bauteil1.D6_PWM
  N5: R5.Pin_0, Bauteil1.D5_PWM
  N6: R6.Pin_0, Bauteil1.D4
  N7: R7.Pin_0, Bauteil1.D3_PWM
  N8: R8.Pin_0, Bauteil1.D2

notes:
  LAUFLICHT

// code stored in the sketch: Lauflicht.ino
/*
  Lauflicht
  
  Dieses Beispiel aus dem Fritzing Creator Kit: www.fritzing.org/creator-kit.
*/

int pinsGesamt=8;                        // deklariert die ganzzahlige Variable pinsGesamt
int pins[] = {2,3,4,5,6,7,8,9};          // deklariert das Array pins[]

void setup() {                
  for (int i=0; i<pinsGesamt; i=i+1){    // zählt die Variable i von 0 bis 7
    pinMode(pins[i], OUTPUT);            // initialisiert den Pin an der pins-Array-Stelle i als OUTPUT
  }
}

void loop() {
  for (int i=0; i<pinsGesamt; i=i+1){    // Lauflicht Hin
    digitalWrite(pins[i], HIGH);         // LED an der Stelle i einschalten
    delay(100);                          // hält das Programm für 100 Millisekunden an
    digitalWrite(pins[i], LOW);          // LED an der Stelle i ausschalten
  }
  for (int i=6; i>0; i=i-1){             // Lauflicht Zurück (die äußeren LEDs werden nicht angesteuert)
    digitalWrite(pins[i], HIGH);         // LED an der Stelle i einschalten
    delay(100);                          // hält das Programm für 100 Millisekunden an
    digitalWrite(pins[i], LOW);          // LED an der Stelle i ausschalten
  }
}
