# Fritzing sketch Potentiometer (saved by Fritzing 1.0.8)
circuit board: 6.88566cm x 5.36311cm
breadboards: 2

parts:
  R1 = Resistor [tolerance=±5% resistance=220 power=0.25W package=THT]
  R2 = Resistor [tolerance=±5% resistance=220 power=0.25W package=THT]
  Arduino1 = Arduino Uno (Rev3)
  R3 = Rotary Potentiometer (Small) [maximum_resistance=100kΩ knob_status=50% power=0.5W package=THT]
  part = LED - 5mm [color="Red (633nm)" current=0.030A package="5 mm [THT]"]  # not connected
  part_2 = LED - 5mm [color="Red (633nm)" current=0.030A package="5 mm [THT]"]  # not connected

nets:
  N1: R1.Pin_1, R2.Pin_1, Arduino1.GND, R3.leg1
  N2: Arduino1.A0, R3.wiper
  N3: Arduino1.5V, R3.leg2

notes:
  POTENTIOMETER

// code stored in the sketch: Potentiometer.ino
/*
  Potentiometer
  zwei LEDs werden mit einem Potentiometer gesteuert
  
  Dieses Beispiel aus dem Fritzing Creator Kit: www.fritzing.org/creator-kit.
*/

int ledGreen = 6;                            // LED Pin wird deklariert
int ledRed = 5;                              // LED Pin wird deklariert
int potPin = 0;                              // Potentiometer wird deklariert

void setup(){
                                             // werder analoge Ein- noch Ausgaben müssen im Setup initialisiert werden
}

void loop(){
  int value = analogRead(potPin);            // die Variable value speichert den Wert des Potentiometers
  int redValue = map(value,0,1023,0,255);    // diser wird mit der Map-Funktion umgerechnet - hier von 0 bis 255,
  int greenValue = map(value,0,1023,255,0);  // hier von 255 - 0
  
  analogWrite(ledRed,redValue);              // die umgerechneten Werte
  analogWrite(ledGreen,greenValue);          // werden an beide LEDs gesendet
}
