# Fritzing sketch Wahrsager (saved by Fritzing 1.0.8)
circuit board: 6.88566cm x 5.36311cm
breadboards: 2

parts:
  R1 = Resistor [tolerance=±5% resistance=100k power=0.25W package=THT]
  Tilt = Tilt Switch [package=THT]
  R4 = Resistor [tolerance=±5% resistance=220 power=0.25W package=THT]
  R5 = Resistor [tolerance=±5% resistance=220 power=0.25W package=THT]
  R6 = Resistor [tolerance=±5% resistance=220 power=0.25W package=THT]
  R2 = Resistor [tolerance=±5% resistance=220 power=0.25W package=THT]
  R3 = Resistor [tolerance=±5% resistance=220 power=0.25W package=THT]
  Arduino1 = Arduino Uno (Rev3)
  part = LED - 5mm [color="Red (633nm)" current=0.030A package="5 mm [THT]"]  # not connected
  part_2 = LED - 5mm [color="Red (633nm)" current=0.030A package="5 mm [THT]"]  # not connected
  part_3 = LED - 5mm [color="Red (633nm)" current=0.030A package="5 mm [THT]"]  # not connected
  part_4 = LED - 5mm [color="Red (633nm)" current=0.030A package="5 mm [THT]"]  # not connected
  part_5 = LED - 5mm [color="Red (633nm)" current=0.030A package="5 mm [THT]"]  # not connected

nets:
  N1: R1.Pin_0, Tilt.Pin_2, Arduino1.D3_PWM
  N2: R1.Pin_1, Arduino1.5V
  N3: Tilt.Pin_1, Arduino1.GND
  N4: R4.Pin_1, Arduino1.D10_PWM/SS
  N5: R5.Pin_1, Arduino1.D9_PWM
  N6: R6.Pin_1, Arduino1.D8
  N7: R2.Pin_1, Arduino1.D12/MISO
  N8: R3.Pin_1, Arduino1.D11_PWM/MOSI

notes:
  WAHRSAGER

// code stored in the sketch: Wahrsager.ino
/*
  Wahrsager
  schaltet zwischen fünf LEDs um die Zukunft vorher zu sagen
  
  Dieses Beispiel aus dem Fritzing Creator Kit: www.fritzing.org/creator-kit.
*/

int pins[] = {8,9,10,11,12};            // Pins der einzelnen LEDs werden in einem Array gespeichert
int tiltPin = 3;                        // Pin-Nummer des Neigungsschalters wird deklariert

void setup() {                           
  for (int i=0; i<5; i=i+1){            
    pinMode(pins[i] , OUTPUT);          // LED Pins werden als OUTPUTS deklariert
  }
  pinMode(tiltPin,INPUT);  // Pin des Neigungsschalters wird als INPUT deklariert
  randomSeed(analogRead(0));
}

void loop() {
  if (digitalRead(tiltPin)==HIGH){      // wenn der Tilt-Switch geöffnet ist
   for (int i=0; i<5; i=i+1){           // werden alle LEDs
     digitalWrite(pins[i],LOW);         // abgeschalten
   }                                    // sonst
   int myRandom=random(0,5);            // eine zufällige LED wird ausgewählt
   digitalWrite(pins[myRandom],HIGH);   // und angeschalten
   delay(20);                           // Programm macht eine kurze Pause
  }
}
