# Fritzing sketch AutomaticLightingSystem (saved by Fritzing 1.0.8)
circuit board: 6.88566cm x 5.36311cm
breadboards: 2

parts:
  R1 = Resistor [tolerance=±5% resistance=220 power=0.25W package=THT]
  R2 = Resistor [tolerance=±5% resistance=220 power=0.25W package=THT]
  Photo_Resistor = Photocell (LDR) [power=0.25W dark_resistance_@0.01lx=300kΩ light_resistance_@100lx=400Ω luminance=10lx package=THT]
  R3 = Resistor [tolerance=±5% resistance=100k power=0.25W package=THT]
  Bauteil1 = Arduino Uno (Rev3)
  part = LED - 5mm [color="Red (633nm)" current=0.030A package="5 mm [THT]"]  # not connected
  part_2 = LED - 5mm [color="Red (633nm)" current=0.030A package="5 mm [THT]"]  # not connected

nets:
  N1: R1.Pin_1, R2.Pin_1, Photo_Resistor.pin_0, Bauteil1.GND
  N2: Photo_Resistor.pin_1, R3.Pin_0, Bauteil1.A0
  N3: R3.Pin_1, Bauteil1.5V

notes:
  LIGHTING SYSTEM

// code stored in the sketch: AutomaticLightingSystem.ino
/*
  Automatic Lighting System
  schaltet die Lichter eines Autos ja nach Helligkeit an und ab
  
  Dieses Beispiel aus dem Fritzing Creator Kit: www.fritzing.org/creator-kit.
*/

int lichtsensorPin = 0;                            // lichtsensorPin wird deklariert
int scheinwerferPin = 2;                           // scheinwerferPin wird deklariert
int schaltgrenze = 300;                            // ab diesem Wert wird »Dunkelheit« definiert
int wartezeit = 1000;                              // Timer-Timeout sind 1000 Millisekunden
long timer = 0;                                    // Timervariabel wird deklariert
int lichtwert;                                     // speichert die Lichtsittuation

void setup(){
  Serial.begin(9600);                              // startet die serielle Kommunikation
  pinMode(scheinwerferPin,OUTPUT);                 // scheinwerferPin wird als OUTPUT initialisiert
}

void loop(){
  lichtwert = analogRead(lichtsensorPin);          // lichtwert wird eingelesen
  Serial.println(lichtwert);                       // lichtwert wird an die serielle Schnittstelle gesendet
  if (lichtwert>schaltgrenze){                     // wenn die Schaltgrenze unterschritten wird
    timer=millis();                                // timer wird auf aktuelle Zeit gesetzt
    digitalWrite(scheinwerferPin, HIGH);           // Scheinwerfer werden eingeschalten
  } else if (millis()>wartezeit+timer){            // sonst wenn er Timer abgelaufen ist
    digitalWrite(scheinwerferPin, LOW);            // werden die Scheinwerfer abgeschalten
  }
  delay(10);                                       // Pause
}
