# Fritzing sketch Fortuneteller (saved by Fritzing 1.0.8)
circuit board: 6.88566cm x 5.36311cm
breadboards: 2

parts:
  R1 = Resistor [tolerance=±5% resistance=100k power=0.25W package=THT]
  Tilt = Tilt Switch [package=THT]
  R4 = Resistor [tolerance=±5% resistance=220 power=0.25W package=THT]
  R5 = Resistor [tolerance=±5% resistance=220 power=0.25W package=THT]
  R6 = Resistor [tolerance=±5% resistance=220 power=0.25W package=THT]
  R2 = Resistor [tolerance=±5% resistance=220 power=0.25W package=THT]
  R3 = Resistor [tolerance=±5% resistance=220 power=0.25W package=THT]
  Arduino1 = Arduino Uno (Rev3)
  part = LED - 5mm [color="Red (633nm)" current=0.030A package="5 mm [THT]"]  # not connected
  part_2 = LED - 5mm [color="Red (633nm)" current=0.030A package="5 mm [THT]"]  # not connected
  part_3 = LED - 5mm [color="Red (633nm)" current=0.030A package="5 mm [THT]"]  # not connected
  part_4 = LED - 5mm [color="Red (633nm)" current=0.030A package="5 mm [THT]"]  # not connected
  part_5 = LED - 5mm [color="Red (633nm)" current=0.030A package="5 mm [THT]"]  # not connected

nets:
  N1: R1.Pin_0, Tilt.Pin_2, Arduino1.D3_PWM
  N2: R1.Pin_1, Arduino1.5V
  N3: Tilt.Pin_1, Arduino1.GND
  N4: R4.Pin_1, Arduino1.D10_PWM/SS
  N5: R5.Pin_1, Arduino1.D9_PWM
  N6: R6.Pin_1, Arduino1.D8
  N7: R2.Pin_1, Arduino1.D12/MISO
  N8: R3.Pin_1, Arduino1.D11_PWM/MOSI

notes:
  FORTUNETELLER

// code stored in the sketch: Fortuneteller.ino
/*
  fortune teller
  switching between five LEDs to tell the future
  
  This example is part of the Fritzing Creator Kit: www.fritzing.org/creatorkit.
*/

int pins[] = {8,9,10,11,12};            // the pins of the LEDs are stored in an array
int tiltPin = 3;                        // pin number where the tilt switch is attached

void setup() {                           
  for (int i=0; i<5; i=i+1){            
    pinMode(pins[i] , OUTPUT);          // LED pins are declared as outputs
  }
  pinMode(tiltPin,INPUT);               // pin of the tilt switch is declared as input
  randomSeed(analogRead(0));            // initialize random number generator based on random state of pin zero
}

void loop() {
  if (digitalRead(tiltPin)==HIGH){      // when the tilt switch is open
   for (int i=0; i<5; i=i+1){           // all the LEDs
     digitalWrite(pins[i],LOW);         // get switched off
   }                                    // 
   int myRandom=random(0,5);            // a random LED 
   digitalWrite(pins[myRandom],HIGH);   // is switched on
   delay(20);                           // the program is waiting to breath
  }
}
