# Fritzing sketch H-Bridge (saved by Fritzing 1.0.8)
circuit board: 6.88566cm x 5.36311cm
breadboards: 2

parts:
  L293D = L293D [package=THT]
  Motor2 = DC Motor [voltage_(max)=6V voltage_(min)=3V]
  VCC = Battery block 9V [internal_resistance=0.1Ω]
  Motor1 = DC Motor [voltage_(max)=6V voltage_(min)=3V]
  Part1 = Arduino Uno (Rev3)

nets:
  N1: L293D.Enable_1, Part1.D3_PWM
  N2: L293D.In_1, Part1.D6_PWM
  N3: L293D.Out_1_(_Controlled_by_Enable_1_), Motor2.pin_2
  N4: L293D.0V, VCC.-, Part1.GND
  N5: L293D.Out_2_(_Controlled_by_Enable_1_), Motor2.pin_1
  N6: L293D.In_2, Part1.D5_PWM
  N7: L293D.+Vmotor, VCC.+, Part1.VIN
  N8: L293D.Enable_2, Part1.D9_PWM
  N9: L293D.In_3, Part1.D11_PWM/MOSI
  N10: L293D.Out_3_(_Controlled_by_Enable_2_), Motor1.pin_2
  N11: L293D.Out_4_(_Controlled_by_Enable_2_), Motor1.pin_1
  N12: L293D.In_4, Part1.D10_PWM/SS
  N13: L293D.+V, Part1.5V

notes:
  H-BRIDGE
