# Fritzing sketch Potentiometer (saved by Fritzing 1.0.8)
circuit board: 6.88566cm x 5.36311cm
breadboards: 2

parts:
  R1 = Resistor [tolerance=±5% resistance=220 power=0.25W package=THT]
  R2 = Resistor [tolerance=±5% resistance=220 power=0.25W package=THT]
  Arduino1 = Arduino Uno (Rev3)
  R6 = Rotary Potentiometer (Small) [maximum_resistance=100kΩ knob_status=50% power=0.5W package=THT]
  part = LED - 5mm [color="Red (633nm)" current=0.030A package="5 mm [THT]"]  # not connected
  part_2 = LED - 5mm [color="Red (633nm)" current=0.030A package="5 mm [THT]"]  # not connected

nets:
  N1: R1.Pin_1, R2.Pin_1, Arduino1.GND, R6.leg1
  N2: Arduino1.A0, R6.wiper
  N3: Arduino1.5V, R6.leg2

notes:
  POTENTIOMETER

// code stored in the sketch: Potentiometer.ino
/*
  potentiometer
  two LEDs are controlled by a potentiometer
  
  This example is part of the Fritzing Creator Kit: www.fritzing.org/creator-kit.
*/

int ledGreen = 6;                            // LED pin is declared
int ledRed = 5;                              // LED pin is declared
int potPin = 0;                              // potentiometer pin is declared

void setup(){
                                             // neither analog inputs nor outputs have to be declared in the setup
}

void loop(){
  int value = analogRead(potPin);            // this variable stores the value from the potentiometer
  int redValue = map(value,0,1023,0,255);    // mapped from a range of 0 to 1023 to a range of 0 to 255 for the red LED,
  int greenValue = map(value,0,1023,255,0);  // and for the green mapped to the reverse range from 255 to 0
  
  analogWrite(ledRed,redValue);              // the recalculated values are
  analogWrite(ledGreen,greenValue);          // send to the LEDs as analog values
}
