# Fritzing sketch Workshop_02_FlipFlop (saved by Fritzing 1.0.8)
circuit board: 6.88566cm x 5.36311cm
breadboards: 2

parts:
  R1 = Resistor [tolerance=±5% resistance=220 power=0.25W package=THT]
  R2 = Resistor [tolerance=±5% resistance=220 power=0.25W package=THT]
  Bauteil1 = Arduino Uno (Rev3)
  part = LED - 5mm [color="Red (633nm)" current=0.030A package="5 mm [THT]"]  # not connected
  part_2 = LED - 5mm [color="Red (633nm)" current=0.030A package="5 mm [THT]"]  # not connected

nets:
  N1: R1.Pin_0, Bauteil1.D10_PWM/SS
  N2: R2.Pin_0, Bauteil1.D9_PWM

notes:
  FLIP FLOP

// code stored in the sketch: Workshop_02_FlipFlop.ino
int greenLED=9;
int redLED=10;

void setup(){
  pinMode(greenLED, OUTPUT);
  pinMode(redLED, OUTPUT);
}
void loop(){
  delay(1000);
  digitalWrite(greenLED, HIGH);
  digitalWrite(redLED, LOW);
  delay(1000);
  digitalWrite(greenLED, LOW);
  digitalWrite(redLED, HIGH);
}
