# Fritzing sketch Workshop_03_FlipFlop-w-Button (saved by Fritzing 1.0.8)
circuit board: 6.88566cm x 5.36311cm
breadboards: 2

parts:
  R3 = Resistor [tolerance=±5% resistance=100k power=0.25W package=THT]
  R1 = Resistor [tolerance=±5% resistance=220 power=0.25W package=THT]
  R2 = Resistor [tolerance=±5% resistance=220 power=0.25W package=THT]
  Button = Pushbutton [package=THT]
  Bauteil1 = Arduino Uno (Rev3)
  part = LED - 5mm [color="Red (633nm)" current=0.030A package="5 mm [THT]"]  # not connected
  part_2 = LED - 5mm [color="Red (633nm)" current=0.030A package="5 mm [THT]"]  # not connected

nets:
  N1: R3.Pin_0, Button.leg1, Bauteil1.D2
  N2: R3.Pin_1, Bauteil1.5V
  N3: R1.Pin_0, Bauteil1.D10_PWM/SS
  N4: R2.Pin_0, Bauteil1.D9_PWM
  N5: Button.leg0, Bauteil1.GND

notes:
  FLIP FLOP

// code stored in the sketch: Workshop_03_FlipFlop-w-Button.ino
int buttonPin=2;
int greenLED=9;
int redLED=10;

void setup(){
  pinMode(buttonPin, INPUT);
  pinMode(greenLED, OUTPUT);
  pinMode(redLED, OUTPUT);
}
void loop(){
  if (digitalRead(buttonPin)==LOW){
    digitalWrite(greenLED, HIGH);
    digitalWrite(redLED, LOW);
  } 
  else {
    digitalWrite(greenLED, LOW);
    digitalWrite(redLED, HIGH);
  }
}
