# Fritzing sketch Workshop_05_Potentiometer (saved by Fritzing 1.0.8)
circuit board: 6.88566cm x 5.36311cm
breadboards: 2

parts:
  R1 = Resistor [tolerance=±5% resistance=220 power=0.25W package=THT]
  R2 = Resistor [tolerance=±5% resistance=220 power=0.25W package=THT]
  Bauteil1 = Arduino Uno (Rev3)
  R3 = Rotary Potentiometer (Small) [maximum_resistance=100kΩ knob_status=50% power=0.5W package=THT]
  part = LED - 5mm [color="Red (633nm)" current=0.030A package="5 mm [THT]"]  # not connected
  part_2 = LED - 5mm [color="Red (633nm)" current=0.030A package="5 mm [THT]"]  # not connected

nets:
  N1: R1.Pin_0, Bauteil1.D10_PWM/SS
  N2: R2.Pin_0, Bauteil1.D9_PWM
  N3: Bauteil1.A0, R3.wiper
  N4: Bauteil1.GND, R3.leg1
  N5: Bauteil1.5V, R3.leg2

notes:
  FLIP FLOP

// code stored in the sketch: Workshop_05_Potentiometer.ino
int ledGreen = 9;
int ledRed = 10;
int potPin = 0;

void setup(){

}

void loop () {
  int value = analogRead(potPin);
  int redValue = map(value,0,1023,0,255);
  int greenValue = map(value,0,1023,255,0);
  analogWrite(ledRed,redValue);
  analogWrite(ledGreen,greenValue);
}
