# Fritzing sketch Workshop_06_Automatic-Lightning (saved by Fritzing 1.0.8)
circuit board: 6.88566cm x 5.36311cm
breadboards: 2

parts:
  R1 = Resistor [tolerance=±5% resistance=220 power=0.25W package=THT]
  R2 = Resistor [tolerance=±5% resistance=220 power=0.25W package=THT]
  Bauteil1 = Arduino Uno (Rev3)
  R4 = Resistor [tolerance=±5% resistance=10k power=0.25W package=THT]
  R5 = Photocell (LDR) [power=0.25W dark_resistance_@0.01lx=300kΩ light_resistance_@100lx=400Ω luminance=10lx package=THT]
  part = LED - 5mm [color="Red (633nm)" current=0.030A package="5 mm [THT]"]  # not connected
  part_2 = LED - 5mm [color="Red (633nm)" current=0.030A package="5 mm [THT]"]  # not connected

nets:
  N1: R1.Pin_0, Bauteil1.D10_PWM/SS
  N2: R2.Pin_0, Bauteil1.D9_PWM
  N3: Bauteil1.A0, R4.Pin_1, R5.pin_0
  N4: Bauteil1.GND, R5.pin_1
  N5: Bauteil1.5V, R4.Pin_0

notes:
  FLIP FLOP

// code stored in the sketch: Workshop_06_Automatic-Lightning.ino
int lightsensorPin = 0;
int headlightsPin1 = 9;
int headlightsPin2 = 10;
int switchingthreshold= 300;
int wait = 1000;
long timer = 0;
int value;

void setup(){
  //Serial.begin(9600);
  pinMode(headlightsPin1,OUTPUT);
  pinMode(headlightsPin2,OUTPUT);
}

void loop(){
  value = analogRead(lightsensorPin);
  //Serial.println(value);
  
  if (value<switchingthreshold){
    timer=millis();
    digitalWrite(headlightsPin1, HIGH);
    digitalWrite(headlightsPin2, HIGH);
  } 
  else if (millis()>wait+timer){
    digitalWrite(headlightsPin1, LOW);
    digitalWrite(headlightsPin2, LOW);    
  }
  
  delay(15); 
}
