# Fritzing sketch Workshop_07_Servo (saved by Fritzing 1.0.8)
circuit board: 6.88566cm x 5.36311cm
breadboards: 2

parts:
  R1 = Resistor [tolerance=±5% resistance=220 power=0.25W package=THT]
  R2 = Resistor [tolerance=±5% resistance=220 power=0.25W package=THT]
  Bauteil1 = Arduino Uno (Rev3)
  R4 = Resistor [tolerance=±5% resistance=10k power=0.25W package=THT]
  R5 = Photocell (LDR) [power=0.25W dark_resistance_@0.01lx=300kΩ light_resistance_@100lx=400Ω luminance=10lx package=THT]
  J1 = Basic Servo
  part = LED - 5mm [color="Red (633nm)" current=0.030A package="5 mm [THT]"]  # not connected
  part_2 = LED - 5mm [color="Red (633nm)" current=0.030A package="5 mm [THT]"]  # not connected

nets:
  N1: R1.Pin_0, Bauteil1.D10_PWM/SS
  N2: R2.Pin_0, Bauteil1.D9_PWM
  N3: Bauteil1.A0, R4.Pin_1, R5.pin_0
  GND: Bauteil1.GND, R5.pin_1, J1.gnd
  N4: Bauteil1.D6_PWM, J1.pulse
  5V: Bauteil1.5V, R4.Pin_0, J1.vcc

notes:
  FLIP FLOP

// code stored in the sketch: Workshop_07_Servo.ino
#include <Servo.h>

Servo myservo;
int potpin = 0;
int val;

void setup()
{
  Serial.begin(9600);
  myservo.attach(6);
}

void loop() {
  val = analogRead(potpin);
  Serial.println(val);
  
  val = map(val, 0, 1023, 0, 179);
  
  myservo.write(val);
  
  delay(100);
}
