# Fritzing sketch Loop (saved by Fritzing 1.0.8)
circuit board: 6.88566cm x 5.36311cm
breadboards: 2

parts:
  R4 = Resistor [resistance=220 tolerance=±5% power=0.25W package=THT]
  R3 = Resistor [resistance=220 tolerance=±5% power=0.25W package=THT]
  R1 = Resistor [resistance=220 tolerance=±5% power=0.25W package=THT]
  R2 = Resistor [resistance=220 tolerance=±5% power=0.25W package=THT]
  R5 = Resistor [resistance=220 tolerance=±5% power=0.25W package=THT]
  R6 = Resistor [resistance=220 tolerance=±5% power=0.25W package=THT]
  Arduino = Arduino Uno (Rev3)
  part = LED - 5mm [color="Red (633nm)" current=0.030A package="5 mm [THT]"]  # not connected
  part_2 = LED - 5mm [color="Red (633nm)" current=0.030A package="5 mm [THT]"]  # not connected
  part_3 = LED - 5mm [color="Red (633nm)" current=0.030A package="5 mm [THT]"]  # not connected
  part_4 = LED - 5mm [color="Red (633nm)" current=0.030A package="5 mm [THT]"]  # not connected
  part_5 = LED - 5mm [color="Red (633nm)" current=0.030A package="5 mm [THT]"]  # not connected
  part_6 = LED - 5mm [color="Red (633nm)" current=0.030A package="5 mm [THT]"]  # not connected

nets:
  N1: R4.Pin_1, Arduino.D5_PWM
  N2: R3.Pin_1, Arduino.D4
  N3: R1.Pin_1, Arduino.D2
  N4: R2.Pin_1, Arduino.D3_PWM
  N5: R5.Pin_1, Arduino.D6_PWM
  N6: R6.Pin_1, Arduino.D7

notes:
  In this example, six leds are controlled by digital out pins. Related Example: http://arduino.cc/en/Tutorial/Loop

// code stored in the sketch: Loop.ino
/*
  For Loop Iteration
 
 Demonstrates the use of a for() loop. 
 Lights multiple LEDs in sequence, then in reverse.
 
 The circuit:
 * LEDs from pins 2 through 7 to ground
 
 created 2006
 by David A. Mellis
 modified 30 Aug 2011
 by Tom Igoe 

This example code is in the public domain.
 
 http://www.arduino.cc/en/Tutorial/ForLoop
 */

int timer = 100;           // The higher the number, the slower the timing.

void setup() {
  // use a for loop to initialize each pin as an output:
  for (int thisPin = 2; thisPin < 8; thisPin++)  {
    pinMode(thisPin, OUTPUT);      
  }
}

void loop() {
  // loop from the lowest pin to the highest:
  for (int thisPin = 2; thisPin < 8; thisPin++) { 
    // turn the pin on:
    digitalWrite(thisPin, HIGH);   
    delay(timer);                  
    // turn the pin off:
    digitalWrite(thisPin, LOW);    
  }

  // loop from the highest pin to the lowest:
  for (int thisPin = 7; thisPin >= 2; thisPin--) { 
    // turn the pin on:
    digitalWrite(thisPin, HIGH);
    delay(timer);
    // turn the pin off:
    digitalWrite(thisPin, LOW);
  }
}
