# Fritzing sketch Optocoupler (saved by Fritzing 1.0.8)
circuit board: 6.88566cm x 5.36311cm
breadboards: 2

parts:
  R3 = Resistor [resistance=220 tolerance=±5% power=0.25 package=THT]
  R4 = Resistor [resistance=220 tolerance=±5% power=0.25 package=THT]
  VCC1 = Battery [internal_resistance=0.1Ω]
  Arduino2 = Arduino Uno (Rev3)
  U1 = Optocoupler [package=THT]
  part = LED - 5mm [color="Red (633nm)" current=0.030A package="5 mm [THT]"]  # not connected

nets:
  N1: R3.Pin_0, Arduino2.D11_PWM/MOSI
  N2: R3.Pin_1, U1.Pin_1
  N3: R4.Pin_1, VCC1.+
  N4: VCC1.-, U1.Pin_4
  N5: Arduino2.GND, U1.Pin_2

notes:
  An optocoupler can be used to control a circuit that's completely isolated from your microcontroller in order to avoid the risk of short-circuit. In this case, imagine that the LED + battery pack combo is a hacked toy that you're turning on and off with the Arduino.
