# Fritzing sketch Parking-Assistant (saved by Fritzing 1.0.8)
circuit board: 6.88566cm x 5.36311cm
breadboards: 2

parts:
  220Ω1 = Resistor [resistance=220 tolerance=±5% power=0.25W package=THT]
  220Ω2 = Resistor [resistance=220 tolerance=±5% power=0.25W package=THT]
  220Ω3 = Resistor [resistance=220 tolerance=±5% power=0.25W package=THT]
  220Ω4 = Resistor [resistance=220 tolerance=±5% power=0.25W package=THT]
  220Ω5 = Resistor [resistance=220 tolerance=±5% power=0.25W package=THT]
  220Ω6 = Resistor [resistance=220 tolerance=±5% power=0.25W package=THT]
  220Ω7 = Resistor [resistance=220 tolerance=±5% power=0.25W package=THT]
  220Ω8 = Resistor [resistance=220 tolerance=±5% power=0.25W package=THT]
  220Ω9 = Resistor [resistance=220 tolerance=±5% power=0.25W package=THT]
  220Ω10 = Resistor [resistance=220 tolerance=±5% power=0.25W package=THT]
  Arduino1 = Arduino Uno (Rev3)
  J1 = Infrared Proximity Sensor [distance_to_obstacle=50%]
  J2 = Infrared Proximity Sensor [distance_to_obstacle=50%]
  part = LED - 5mm [color="Red (633nm)" current=0.030A package="5 mm [THT]"]  # not connected
  part_2 = LED - 5mm [color="Red (633nm)" current=0.030A package="5 mm [THT]"]  # not connected
  part_3 = LED - 5mm [color="Red (633nm)" current=0.030A package="5 mm [THT]"]  # not connected
  part_4 = LED - 5mm [color="Red (633nm)" current=0.030A package="5 mm [THT]"]  # not connected
  part_5 = LED - 5mm [color="Red (633nm)" current=0.030A package="5 mm [THT]"]  # not connected
  part_6 = LED - 5mm [color="Red (633nm)" current=0.030A package="5 mm [THT]"]  # not connected
  part_7 = LED - 5mm [color="Red (633nm)" current=0.030A package="5 mm [THT]"]  # not connected
  part_8 = LED - 5mm [color="Red (633nm)" current=0.030A package="5 mm [THT]"]  # not connected
  part_9 = LED - 5mm [color="Red (633nm)" current=0.030A package="5 mm [THT]"]  # not connected
  part_10 = LED - 5mm [color="Red (633nm)" current=0.030A package="5 mm [THT]"]  # not connected

nets:
  N1: 220Ω1.Pin_1, Arduino1.D5_PWM
  N2: 220Ω2.Pin_1, Arduino1.D3_PWM
  N3: 220Ω3.Pin_1, Arduino1.D4
  N4: 220Ω4.Pin_1, Arduino1.D6_PWM
  N5: 220Ω5.Pin_1, Arduino1.D7
  N6: 220Ω6.Pin_1, Arduino1.D9_PWM
  N7: 220Ω7.Pin_1, Arduino1.D8
  N8: 220Ω8.Pin_1, Arduino1.D10_PWM/SS
  N9: 220Ω9.Pin_1, Arduino1.D11_PWM/MOSI
  N10: 220Ω10.Pin_1, Arduino1.D12/MISO
  N11: Arduino1.A0, J1.Vout
  N12: Arduino1.A1, J2.Vout
  GND: Arduino1.GND, J1.GND, J2.GND
  VCC: Arduino1.5V, J1.Vcc, J2.Vcc

notes:
  Simple Parking Assistant
  The distance to objects in the proximity is measured and displayed as led graph.
