# Fritzing sketch Shift_Register (saved by Fritzing 1.0.8)
circuit board: 6.88566cm x 5.36311cm
breadboards: 2

parts:
  R10 = Resistor [resistance=220 tolerance=±5% power=0.25W package=THT]
  R11 = Resistor [resistance=220 tolerance=±5% power=0.25W package=THT]
  R12 = Resistor [resistance=220 tolerance=±5% power=0.25W package=THT]
  R13 = Resistor [resistance=220 tolerance=±5% power=0.25W package=THT]
  R14 = Resistor [resistance=220 tolerance=±5% power=0.25W package=THT]
  R15 = Resistor [resistance=220 tolerance=±5% power=0.25W package=THT]
  R16 = Resistor [resistance=220 tolerance=±5% power=0.25W package=THT]
  R17 = Resistor [resistance=220 tolerance=±5% power=0.25W package=THT]
  74HC5952 = 74HC595 [package="DIP16 [THT]"]
  C3 = Ceramic Capacitor [capacitance=100nF rated_voltage=35V package="200 mil [THT, multilayer]"]
  Arduino1 = Arduino Uno (Rev3)
  part = LED - 5mm [color="Red (633nm)" current=0.030A package="5 mm [THT]"]  # not connected
  part_2 = LED - 5mm [color="Red (633nm)" current=0.030A package="5 mm [THT]"]  # not connected
  part_3 = LED - 5mm [color="Red (633nm)" current=0.030A package="5 mm [THT]"]  # not connected
  part_4 = LED - 5mm [color="Red (633nm)" current=0.030A package="5 mm [THT]"]  # not connected
  part_5 = LED - 5mm [color="Red (633nm)" current=0.030A package="5 mm [THT]"]  # not connected
  part_6 = LED - 5mm [color="Red (633nm)" current=0.030A package="5 mm [THT]"]  # not connected
  part_7 = LED - 5mm [color="Red (633nm)" current=0.030A package="5 mm [THT]"]  # not connected
  part_8 = LED - 5mm [color="Red (633nm)" current=0.030A package="5 mm [THT]"]  # not connected

nets:
  N1: R10.Pin_1, 74HC5952.Q6
  N2: R11.Pin_1, 74HC5952.Q5
  N3: R12.Pin_1, 74HC5952.Q4
  N4: R13.Pin_1, 74HC5952.Q7
  N5: R14.Pin_1, 74HC5952.Q3
  N6: R15.Pin_1, 74HC5952.Q2
  N7: R16.Pin_1, 74HC5952.Q1
  N8: R17.Pin_1, 74HC5952.Q0
  GND: 74HC5952.GND, 74HC5952.OE, C3.1, Arduino1.GND
  VCC: 74HC5952.MR, 74HC5952.VCC, Arduino1.5V
  N9: 74HC5952.SH_CP, Arduino1.D12/MISO
  N10: 74HC5952.ST_CP, C3.0, Arduino1.D8
  N11: 74HC5952.DS, Arduino1.D11_PWM/MOSI

notes:
  In this project, a 74HC595 shift register is used to control 8 LEDs with just 3 Arduino pins.
  Related example: http://www.arduino.cc/en/Tutorial/ShiftOut

// code stored in the sketch: Shift_Register.ino
/*
  Shift Register Example
 for 74HC595 shift register

 This sketch turns reads serial input and uses it to set the pins
 of a 74HC595 shift register.

 Hardware:
 * 74HC595 shift register attached to pins 2, 3, and 4 of the Arduino,
 as detailed below.
 * LEDs attached to each of the outputs of the shift register

 Created 22 May 2009
 Created 23 Mar 2010
 by Tom Igoe

 */

//Pin connected to latch pin (ST_CP) of 74HC595
const int latchPin = 8;
//Pin connected to clock pin (SH_CP) of 74HC595
const int clockPin = 12;
////Pin connected to Data in (DS) of 74HC595
const int dataPin = 11;

void setup() {
  //set pins to output because they are addressed in the main loop
  pinMode(latchPin, OUTPUT);
  pinMode(dataPin, OUTPUT);  
  pinMode(clockPin, OUTPUT);
  Serial.begin(9600);
  Serial.println("reset");
}

void loop() {
  if (Serial.available() > 0) {
    // ASCII '0' through '9' characters are
    // represented by the values 48 through 57.
    // so if the user types a number from 0 through 9 in ASCII, 
    // you can subtract 48 to get the actual value:
    int bitToSet = Serial.read() - 48;

  // write to the shift register with the correct bit set high:
    registerWrite(bitToSet, HIGH);
  }
}

// This method sends bits to the shift register:

void registerWrite(int whichPin, int whichState) {
// the bits you want to send
  byte bitsToSend = 0;

  // turn off the output so the pins don't light up
  // while you're shifting bits:
  digitalWrite(latchPin, LOW);

  // turn on the next highest bit in bitsToSend:
  bitWrite(bitsToSend, whichPin, whichState);

  // shift the bits out:
  shiftOut(dataPin, clockPin, MSBFIRST, bitsToSend);

    // turn on the output so the LEDs can light up:
  digitalWrite(latchPin, HIGH);

}
