# Fritzing sketch ir_sensor_npn_transistor_dc_motor (saved by Fritzing 1.0.8)
circuit board: 5.75099cm x 2.90545cm
breadboards: 1

parts:
  M1 = fc-51 [package=THT]
  R1 = Resistor [tolerance=±5% power=0.25 resistance=120 package=THT]
  Q1 = NPN-Transistor [package="TO92 [THT]"]
  M2 = DC Motor [voltage_(max)=6V voltage_(min)=2V]
  VCC1 = Battery [internal_resistance=0.1Ω]

nets:
  out_sensor: M1.pin1, R1.Pin_0
  GND: M1.pin2, Q1.E, VCC1.-
  3V: M1.pin3, M2.pin_2, VCC1.+
  N1: R1.Pin_1, Q1.B
  N2: Q1.C, M2.pin_1

notes:
  Press the "Start Simulation" button to start the simulator. It will simulate your circuit when you change your circuit. To stop the simulator, press the "Stop Simulator" button.
  If you do not see the "Start Simulator" button, go to Edit->Preferences and enable the simulator in the "Beta Features" tab.
  Observe the motor turn (or not), based on the status of the sensor.
  The current of the output of the sensor is really small and not enough to make the motor turn. Thus, we need a transistor. The transistor, based on the voltage applied to its base, allows current to flow from the collector to the emiter.
  Add two ammeters and measure the current that flows through the motor and the current that flows from the out pin of the sensor to the base of the transistor.
  Distance Sensor
