# Fritzing sketch measure_dc_current (saved by Fritzing 1.0.8)
breadboards: 1

parts:
  VCC1 = Battery [internal_resistance=0.1Ω]
  R1 = Resistor [tolerance=±5% power=0.25 resistance=220 package=THT]
  AM1 = Multimeter (DC Current)

nets:
  N1: VCC1.-, AM1.COM_Probe
  N2: VCC1.+, R1.Pin_0
  N3: R1.Pin_1, AM1.A_Probe

notes:
  The multimeter measures the current that flows through the resistor.
  Press the "Start Simulation" button to start the simulator. It will simulate your circuit when you change your circuit. To stop the simulator, press the "Stop Simulator" button.
  If you do not see the "Start Simulator" button, go to Edit->Preferences and enable the simulator in the "Beta Features" tab.
  Change the resistance of the resistor to observe how the current changes!
  Change the voltage of the battery to observe how the current changes!
