# Fritzing sketch measure_dc_voltage (saved by Fritzing 1.0.8)
breadboards: 1

parts:
  VM1 = Multimeter (DC Voltage)
  VCC1 = Battery [internal_resistance=0.1Ω]

nets:
  GND: VM1.COM_Probe, VCC1.-
  N1: VM1.V_Probe, VCC1.+

notes:
  You can measure voltages with the voltmeter.
  It measures the voltage of the "V" port with respect to the "COM" port.
  Never connect a cable to the "A" port when the multimeter is reading voltages.
  Change the voltage of the battery in the Inspector pane and observe how the multimeter reads the voltage of the battery.
  Press the "Start Simulation" button to start the simulator. It will simulate your circuit when you change your circuit. To stop the simulator, press the "Stop Simulator" button.
  If you do not see the "Start Simulator" button, go to Edit->Preferences and enable the simulator in the "Beta Features" tab.
