# Fritzing sketch simple_button (saved by Fritzing 1.0.8)
breadboards: 1

parts:
  VCC1 = Battery [internal_resistance=0.1Ω]
  R1 = Resistor [tolerance=±5% power=0.25 resistance=220 package=THT]
  AM1 = Multimeter (DC Voltage)
  S1 = Pushbutton [package=THT]

nets:
  GND: VCC1.-, AM1.COM_Probe, S1.leg0
  N1: VCC1.+, R1.Pin_0
  N2: R1.Pin_1, AM1.V_Probe, S1.leg1

notes:
  The multimeter measures the voltage of a point in the circuit that can be used to determine the status of the button.
  Press the "Start Simulation" button to start the simulator. It will simulate your circuit when you change your circuit. To stop the simulator, press the "Stop Simulator" button.
  If you do not see the "Start Simulator" button, go to Edit->Preferences and enable the simulator in the "Beta Features" tab.
  Change the status of the button in the Inspector pane and observe how the voltage changes!
