# Fritzing sketch simple_led (saved by Fritzing 1.0.8)
circuit board: 3.01251cm x 2.35513cm
breadboards: 1

parts:
  R1 = Resistor [tolerance=±5% power=0.25 resistance=35 package=THT]
  VCC1 = Battery [internal_resistance=0.1Ω]
  part = LED - 5mm [color="Red (633nm)" current=0.030A package="5 mm [THT]"]  # not connected

nets:
  N1: R1.Pin_1, VCC1.+
  GND: VCC1.-

notes:
  Press the "Start Simulation" button to start the simulator. It will simulate your circuit when you change your circuit. To stop the simulator, press the "Stop Simulator" button.
  If you do not see the "Start Simulator" button, go to Edit->Preferences and enable the simulator in the "Beta Features" tab.
  Observe how the LED changes its brithness when you change the voltage of the battery or the resitance of the resistor.
  Take care, a standard LED can only handle 30mA of current. If more current flows through the LED, the LED will be damaged!
