# Fritzing sketch simple_potentiometer (saved by Fritzing 1.0.8)
circuit board: 8.46667cm x 5.64444cm
breadboards: 1

parts:
  VCC1 = Battery [internal_resistance=0.1Ω]
  VM1 = Multimeter (DC Voltage)
  R1 = Rotary Potentiometer (Small) [maximum_resistance=10kΩ knob_status=50% power=0.5W package=THT]

nets:
  GND: VCC1.-, VM1.COM_Probe, R1.leg1
  N1: VCC1.+, R1.leg2
  N2: VM1.V_Probe, R1.wiper

notes:
  Press the "Start Simulation" button to start the simulator. It will simulate your circuit when you change your circuit. To stop the simulator, press the "Stop Simulator" button.
  If you do not see the "Start Simulator" button, go to Edit->Preferences and enable the simulator in the "Beta Features" tab.
  Observe how the voltage changes when you move the knob of the potentiometer (change "knob status" in the Inspector pane).
