# Fritzing sketch 555_IC_astable (saved by Fritzing 1.0.8)
breadboards: 1

parts:
  U1 = 555 Timer [package="DIP8 [THT]"]
  C1 = Ceramic Capacitor [capacitance=100nF voltage=35V package="100 mil [THT, multilayer]"]
  R1 = Resistor [tolerance=±5% power=0.25W resistance=8.2k package=THT]
  VCC1 = Battery block 9V [internal_resistance=0.1Ω]
  C2 = Ceramic Capacitor [capacitance=10µF voltage=35V package="100 mil [THT, multilayer]"]
  Oscilloscope1 = Oscilloscope [volts/div=1V time/div=200ms ch1_offset=0V ch2_offset=0V ch3_offset=0V ch4_offset=0V ch1_volts/div=5V ch2_volts/div=5V ch3_volts/div=5V ch4_volts/div=5V horizontal_position=0s]
  R2 = Resistor [tolerance=±5% power=0.25W resistance=68k package=THT]

nets:
  GND: U1.Ground, C1.0, VCC1.-, C2.0, Oscilloscope1.COM_Probe
  N1: U1.Trigger, U1.Threshold, C2.1, R2.Pin_1
  OUT: U1.Output, Oscilloscope1.V1_Probe
  9V: U1.Reset, U1.Vcc_Supply_Voltage, R1.Pin_0, VCC1.+
  N2: U1.Control_Voltage, C1.1
  N3: U1.Discharge, R1.Pin_1, R2.Pin_0
