# Fritzing sketch oscilloscope_pulse_test (saved by Fritzing 1.0.8)
breadboards: 1

parts:
  Oscilloscope1 = Oscilloscope [volts/div=1V time/div=10ms ch1_offset=5V ch2_offset=0V ch3_offset=10 ch4_offset=-5 ch1_volts/div=5V ch2_volts/div=5V ch3_volts/div=5V ch4_volts/div=5V horizontal_position=0s]
  V2 = Pulse Power [initial_voltage=0V pulsed_voltage=5V period=30m pulse_width=10ms rise_time=0s fall_time=0s number_of_pulses=0 delay_time=0s voltage=5V amplitude=5V offset_voltage=0V internal_resistance=0.1Ω]
  R1 = Resistor [tolerance=±5% power=0.25W resistance=220 package=THT]
  C1 = Ceramic Capacitor [capacitance=8µ voltage=35V package="100 mil [THT, multilayer]"]
  D1 = Rectifier Diode [part_number=1N4001 package="300 mil [THT]"]
  R2 = Resistor [tolerance=±5% power=0.25W resistance=220 package=THT]
  C2 = Ceramic Capacitor [capacitance=8µ voltage=35V package="100 mil [THT, multilayer]"]

nets:
  GND: Oscilloscope1.COM_Probe, V2.V-, C1.1, C2.1
  N1: Oscilloscope1.V1_Probe, R1.Pin_1, C1.0
  N2: Oscilloscope1.V2_Probe, R2.Pin_1, C2.0
  N3: Oscilloscope1.V4_Probe, V2.V+, R1.Pin_0, D1.anode
  N4: D1.cathode, R2.Pin_0
