# Fritzing sketch TemperaturSensorLM35 (saved by Fritzing 1.0.8)
circuit board: 6.88566cm x 5.36311cm
breadboards: 2

parts:
  T2 = LM35 Temperature Sensor [package="TO92 [THT]"]
  R7 = Resistor [tolerance=±5% resistance=220 power=0.25W package=THT]
  R8 = Resistor [tolerance=±5% resistance=220 power=0.25W package=THT]
  R9 = Resistor [tolerance=±5% resistance=220 power=0.25W package=THT]
  R10 = Resistor [tolerance=±5% resistance=220 power=0.25W package=THT]
  R11 = Resistor [tolerance=±5% resistance=220 power=0.25W package=THT]
  R12 = Resistor [tolerance=±5% resistance=220 power=0.25W package=THT]
  Arduino1 = Arduino Uno (Rev3)
  part = LED - 5mm [color="Red (633nm)" current=0.030A package="5 mm [THT]"]  # not connected
  part_2 = LED - 5mm [color="Red (633nm)" current=0.030A package="5 mm [THT]"]  # not connected
  part_3 = LED - 5mm [color="Red (633nm)" current=0.030A package="5 mm [THT]"]  # not connected
  part_4 = LED - 5mm [color="Red (633nm)" current=0.030A package="5 mm [THT]"]  # not connected
  part_5 = LED - 5mm [color="Red (633nm)" current=0.030A package="5 mm [THT]"]  # not connected
  part_6 = LED - 5mm [color="Red (633nm)" current=0.030A package="5 mm [THT]"]  # not connected

nets:
  N1: T2.+Vs, Arduino1.5V
  N2: T2.Vout, Arduino1.A0
  GND: T2.GND, R7.Pin_0, R8.Pin_0, R9.Pin_0, R10.Pin_0, R11.Pin_0, R12.Pin_0, Arduino1.GND

notes:
  Digital Thermometer
  get the code from here
  Digital Thermometer with LM35

// code stored in the sketch: TemperaturSensorLM35.ino
/*

  Sensing the Temperature with the LM35
  Fritzing.org
  
  This script will output the sensed temperature of the LM35 from 20 to 32°C by LEDs.
  
  inspired by
  ladyada http://www.ladyada.net/learn/sensors/tmp36.html
  pscmpf http://pscmpf.blogspot.com/2008/12/arduino-lm35-sensor.html
  
*/

float temperature;                        // stores the temperature
int sensorPin = 0;                        // pin where the sensor is connected to
int startTemp=20;                         // the start temperature > at this temperature, no LED will light up

void setup()
{
  Serial.begin(9600);                     // initialisation of the serial connection
  for (int i=2;i<8; i++){                // output channels from 2 to 7
    pinMode(i,OUTPUT);                    // pin is a output
  }
}

void loop()
{
  temperature = analogRead(sensorPin);    // reading analog sensor value
  temperature = temperature*0.488;        // correcting to °C 

  for (int i=0;i<8; i++){
    if (temperature>((i*2)+startTemp)){       // switch LED on, if temperature is higher than starttemp + (LED number*2)
      digitalWrite(i,HIGH);
    } 
    else {
      digitalWrite(i,LOW);                // else, switch it off
    }
  }

  Serial.print(temperature);Serial.println(" °C");  // send the temperarue to the serial monitor
  delay(500);                             // just wait a little
}
